# Fritzing sketch circuitDiagram (saved by Fritzing 0.9.3b)
breadboards: 1

parts:
  U1 = NodeMCU V1.0
  J1 = Basic Servo
  U2 = LCD-16X2 [package=lcd-16x2_noholes]
  Part2 = KY-037 High Sensitivity Sound Detection Module [package="Breakout board"]
  Part3 = RFID-RC522-v2
  R1 = Trimmer Potentiometer [maximum_resistance=10kΩ package=THT]
  R2 = Trimmer Potentiometer [maximum_resistance=10kΩ package=THT]
  U3 = 74HC595 SMD [package="SO16 [SMD]"]

nets:
  N1: U1.D0, U3.DS
  N2: U1.D1, U3.ST_CP
  N3: U1.D2, U3.SH_CP
  N4: U1.D3, J1.pulse
  N5: U1.D4, Part3.RST
  VCC: U1.3V3, J1.vcc, U2.VDD, Part2.+, Part3.3_3V, R1.leg2, R2.leg2, U3.VCC
  GND: U1.GND, J1.gnd, U2.VSS, U2.R_W, U2.K, Part2.G, Part3.GND, R1.leg1, R2.leg1, U3.GND, U3.OE
  N6: U1.D5, Part3.SCK
  N7: U1.D6, Part3.MISO
  N8: U1.D7, Part3.MOSI
  N9: U1.D8, Part3.SDA
  N10: U1.A0, Part2.A0
  N11: U2.VO, R1.wiper
  N12: U2.RS, U3.Q7
  N13: U2.DB4, U3.Q4
  N14: U2.DB5, U3.Q3
  N15: U2.DB6, U3.Q2
  N16: U2.DB7, U3.Q1
  N17: U2.A, R2.wiper

custom parts:
  NodeMCU V1.0: ESP8266 based NodeMCU
  KY-037 High Sensitivity Sound Detection Module: KY-037 high sensitivity sound detection module is an analog/digital sensor that uses a condenser microphone to observe changes in environment noise.
  RFID-RC522-v2: A simple China made RFID-RC522 Reader; do check the pin labels, as this is a MFRC522 based clone.
